// Logisim project CPU.circ as structural Verilog
module CUPU_II (
  input  [31:0] data_in,
  input  in_2,
  input  in_3,
  output [31:0] data_out,
  output [31:0] address
);

  wire [7:0] bit_extender_1_out, register_2_q;
  wire [31:0] multiplexer_1_out;

  Multiplexer #(.select(2), .width(32)) multiplexer_1 (.out(multiplexer_1_out));  // open: in0, in1, in2, in3, sel
  Register #(.width(32)) register_1 (.D(multiplexer_1_out));  // open: en, Q, clk, clr
  Multiplexer #(.select(2), .width(32)) multiplexer_2 (.out(address));  // open: in0, in1, in2, in3, sel
  Bit_Extender #(.in_width(32), .out_width(8), .\type ("zero")) bit_extender_1 (.in(data_in), .out(bit_extender_1_out));
  Register register_2 (.D(bit_extender_1_out), .Q(register_2_q));  // open: en, clk, clr
  regs regs_1 (.target(register_2_q[3:2]), .source(register_2_q[1:0]));  // open: load, data_in, data_out
endmodule

module regs (
  input  load,
  input  [1:0] target,
  input  [1:0] source,
  input  [31:0] data_in,
  output [31:0] data_out
);

  wire decoder_1_out1, decoder_1_out2, decoder_1_out3;
  wire [31:0] register_1_q, register_2_q, register_3_q;

  Decoder #(.select(2)) decoder_1 (
    .out1(decoder_1_out1), .out2(decoder_1_out2), .out3(decoder_1_out3), .sel(target), .en(load));  // open: out0
  Register #(.width(32)) register_1 (.D(data_in), .Q(register_1_q), .clk(decoder_1_out1));  // open: en, clr
  Register #(.width(32)) register_2 (.D(data_in), .Q(register_2_q), .clk(decoder_1_out2));  // open: en, clr
  Register #(.width(32)) register_3 (.D(data_in), .Q(register_3_q), .clk(decoder_1_out3));  // open: en, clr
  Multiplexer #(.select(2), .width(32)) multiplexer_1 (
    .in0({32{1'b0}}), .in1(register_1_q), .in2(register_2_q), .in3(register_3_q), .out(data_out), .sel(source));
endmodule

module decode (
  input  [7:0] in_1,
  input  [31:0] in_2,
  input  [31:0] in_3
);

  wire [31:0] bit_extender_1_out, bit_extender_2_out, bit_extender_3_out, bit_extender_4_out;

  assign bit_extender_1_out = {{16{in_2[15]}}, in_2[15:0]};  // Bit_Extender bit_extender_1
  assign bit_extender_2_out = {{24{in_2[7]}}, in_2[7:0]};  // Bit_Extender bit_extender_2
  assign bit_extender_3_out = {{16{1'b0}}, in_2[15:0]};  // Bit_Extender bit_extender_3
  assign bit_extender_4_out = {{24{1'b0}}, in_2[7:0]};  // Bit_Extender bit_extender_4
  Multiplexer #(.select(3), .width(32)) multiplexer_1 (
    .in0(in_2), .in1(bit_extender_1_out), .in2(bit_extender_2_out), .in5(bit_extender_3_out),
    .in6(bit_extender_4_out), .sel(in_1[2:0]));  // open: in3, in4, in7, out
endmodule
